// Logisim project proyecto1_arqui_2024.circ as structural Verilog: 1 circuit, main circuit main
module main (
  input  A,
  input  B,
  input  C,
  input  D,
  input  E,
  input  [8:0] in_6
);

  wire and_1_out, and_2_out, and_3_out, and_4_out, and_5_out, and_6_out, and_7_out, and_8_out, and_9_out,
       and_10_out, and_11_out, and_12_out, and_13_out, and_14_out, and_15_out, and_16_out, and_17_out,
       and_18_out, and_19_out, and_20_out, and_21_out, and_22_out, and_23_out, and_24_out, and_25_out,
       and_26_out, and_27_out, and_28_out, and_29_out, and_30_out, and_31_out, and_32_out, and_33_out,
       and_34_out, and_35_out, and_36_out, and_37_out, and_39_out, and_40_out, bcd_to_7_segment_decoder_1_p1,
       bcd_to_7_segment_decoder_1_p2, bcd_to_7_segment_decoder_1_p3, bcd_to_7_segment_decoder_1_p4,
       bcd_to_7_segment_decoder_1_p5, bcd_to_7_segment_decoder_1_p6, bcd_to_7_segment_decoder_1_p7,
       bcd_to_7_segment_decoder_1_p8, bcd_to_7_segment_decoder_2_p1, bcd_to_7_segment_decoder_2_p2,
       bcd_to_7_segment_decoder_2_p3, bcd_to_7_segment_decoder_2_p4, bcd_to_7_segment_decoder_2_p5,
       bcd_to_7_segment_decoder_2_p6, bcd_to_7_segment_decoder_2_p7, bcd_to_7_segment_decoder_2_p8,
       bcd_to_7_segment_decoder_3_p1, bcd_to_7_segment_decoder_3_p2, bcd_to_7_segment_decoder_3_p3,
       bcd_to_7_segment_decoder_3_p4, bcd_to_7_segment_decoder_3_p6, bcd_to_7_segment_decoder_3_p7,
       bcd_to_7_segment_decoder_3_p8, binary_to_bcd_converter_1_p5, clock_1_out, decoder_1_out0,
       decoder_1_out2, decoder_1_out4, decoder_1_out7, decoder_1_out11, decoder_1_out12, decoder_1_out13,
       decoder_1_out15, decoder_1_out20, multiplexer_1_out, multiplexer_2_out, multiplexer_3_out, not_1_out,
       not_2_out, not_3_out, not_4_out, not_5_out, not_6_out, not_7_out, not_8_out, not_9_out, not_10_out,
       not_11_out, not_12_out, not_13_out, not_14_out, not_15_out, not_16_out, not_17_out, not_18_out,
       not_19_out, not_20_out, not_21_out, not_22_out, not_23_out, not_24_out, not_25_out, not_26_out,
       not_27_out, not_28_out, not_29_out, not_30_out, not_31_out, not_32_out, not_33_out, not_34_out,
       not_35_out, not_36_out, not_37_out, not_38_out, not_39_out, not_40_out, not_41_out, not_42_out,
       not_43_out, not_44_out, not_45_out, not_46_out, not_47_out, not_48_out, not_49_out, not_50_out,
       or_1_out, or_2_out, or_3_out, or_4_out, or_5_out, or_6_out, or_7_out, or_8_out, or_9_out, or_10_out,
       or_11_out, or_12_out, or_13_out, or_14_out, or_15_out, or_16_out, or_17_out, or_18_out, or_19_out,
       or_20_out, or_21_out, or_22_out, or_23_out, or_24_out, or_25_out, or_26_out, or_27_out, or_28_out;
  wire [8:0] counter_1_q, multiplexer_12_out;

  not not_1 (not_1_out, B);
  not not_2 (not_2_out, D);
  not not_3 (not_3_out, E);
  LED led_1 (.in(or_6_out));
  not not_4 (not_4_out, B);
  not not_5 (not_5_out, D);
  not not_6 (not_6_out, E);
  not not_7 (not_7_out, B);
  not not_8 (not_8_out, D);
  not not_9 (not_9_out, E);
  not not_10 (not_10_out, A);
  not not_11 (not_11_out, B);
  not not_12 (not_12_out, C);
  not not_13 (not_13_out, D);
  not not_14 (not_14_out, E);
  Decoder #(.enable("false"), .select(5)) decoder_1 (
    .out0(decoder_1_out0), .out2(decoder_1_out2), .out4(decoder_1_out4), .out7(decoder_1_out7),
    .out11(decoder_1_out11), .out12(decoder_1_out12), .out13(decoder_1_out13), .out15(decoder_1_out15),
    .out20(decoder_1_out20), .sel({A, B, C, D, E}));  // open: out1, out3, out5, out6, out8, out9, out10, out14, out16, out17, out18, out19, out21, out22, out23, out24, out25, out26, out27, out28, out29, out30, out31
  and and_1 (and_1_out, not_4_out, not_5_out, not_6_out);
  and and_2 (and_2_out, B, not_8_out, not_9_out);
  and and_3 (and_3_out, not_7_out, D, E);
  and and_4 (and_4_out, not_7_out, not_8_out);
  and and_5 (and_5_out, B, D, E);
  and and_6 (and_6_out, not_7_out, D, not_9_out);
  and and_7 (and_7_out, B, not_8_out);
  and and_8 (and_8_out, not_8_out, not_9_out);
  and and_9 (and_9_out, not_4_out, not_5_out, not_6_out);
  and and_10 (and_10_out, B, D);
  and and_11 (and_11_out, not_5_out, not_4_out);
  and and_12 (and_12_out, B, E);
  and and_13 (and_13_out, A, B, not_12_out, not_13_out, E);
  and and_14 (and_14_out, not_10_out, B, not_12_out, D);
  and and_15 (and_15_out, D, B, not_10_out, not_14_out);
  and and_16 (and_16_out, not_10_out, B, C, not_13_out);
  and and_17 (and_17_out, A, C, D, E);
  and and_18 (and_18_out, A, not_11_out, C, E);
  and and_19 (and_19_out, D, E);
  and and_20 (and_20_out, not_2_out, not_3_out);
  and and_21 (and_21_out, not_1_out, E);
  and and_22 (and_22_out, not_1_out, not_2_out);
  or or_1 (or_1_out, and_9_out, and_10_out);
  or or_2 (or_2_out, and_11_out, and_12_out);
  and and_23 (and_23_out, and_11_out, E);
  and and_24 (and_24_out, E, D);
  or or_3 (or_3_out, and_2_out, and_3_out);
  or or_4 (or_4_out, and_5_out, and_6_out);
  or or_5 (or_5_out, and_7_out, and_8_out);
  or or_6 (or_6_out, decoder_1_out0, decoder_1_out2, decoder_1_out4, decoder_1_out7, decoder_1_out11, decoder_1_out12, decoder_1_out13, decoder_1_out15, decoder_1_out20);
  and and_25 (and_25_out, and_19_out, B);
  or or_7 (or_7_out, and_23_out, and_24_out);
  or or_8 (or_8_out, and_24_out, and_1_out);
  and and_26 (and_26_out, B, and_20_out);
  or or_9 (or_9_out, and_20_out, and_21_out, and_22_out);
  or or_10 (or_10_out, and_25_out, and_26_out);
  or or_11 (or_11_out, and_13_out, and_14_out, and_15_out, and_16_out, and_17_out, and_18_out);
  Multiplexer #(.select(2)) multiplexer_1 (
    .in0(and_19_out), .in1(or_10_out), .in2(and_20_out), .in3(or_9_out), .out(multiplexer_1_out), .sel({B, D}));
  Multiplexer #(.select(2)) multiplexer_2 (
    .in0(or_1_out), .in1(or_2_out), .in2(or_7_out), .in3(or_8_out), .out(multiplexer_2_out), .sel({A, C}));
  Multiplexer #(.select(2)) multiplexer_3 (
    .in0(or_3_out), .in1(and_4_out), .in2(or_4_out), .in3(or_5_out), .out(multiplexer_3_out), .sel({A, C}));
  LED led_2 (.in(multiplexer_1_out));
  LED led_3 (.in(multiplexer_2_out));
  LED led_4 (.in(multiplexer_3_out));
  LED led_5 (.in(or_6_out));
  LED led_6 (.in(or_11_out));
  and and_27 (and_27_out, multiplexer_1_out, and_35_out);
  and and_28 (and_28_out, multiplexer_2_out, and_36_out);
  and and_29 (and_29_out, multiplexer_3_out, and_37_out);
  and and_30 (and_30_out, or_6_out, and_34_out);
  and and_31 (and_31_out, or_6_out, and_39_out);
  and and_32 (and_32_out, or_11_out, and_40_out);
  or or_12 (or_12_out, and_27_out, and_28_out, and_29_out, and_32_out);
  Multiplexer multiplexer_4 (.in0(or_12_out), .in1(or_13_out), .out(multiplexer_12_out[8]), .sel(or_12_out));
  or or_13 (or_13_out, and_34_out, and_34_out);
  Multiplexer multiplexer_5 (.in0(or_14_out), .in1(and_34_out), .out(multiplexer_12_out[7]), .sel(or_14_out));
  or or_14 (or_14_out, and_28_out, and_31_out);
  or or_15 (or_15_out, and_27_out, and_28_out, and_29_out, and_31_out, and_32_out);
  Multiplexer multiplexer_6 (.in0(or_15_out), .in1(or_16_out), .out(multiplexer_12_out[6]), .sel(or_15_out));
  or or_16 (or_16_out, and_33_out, and_35_out, and_36_out, and_34_out, and_34_out);
  Multiplexer multiplexer_7 (.in0(or_17_out), .in1(or_18_out), .out(multiplexer_12_out[5]), .sel(or_17_out));
  or or_17 (or_17_out, and_27_out, and_29_out, and_31_out);
  or or_18 (or_18_out, and_33_out, and_36_out, and_34_out);
  or or_19 (or_19_out, and_27_out, and_28_out, and_29_out, and_31_out, and_32_out);
  Multiplexer multiplexer_8 (.in0(or_19_out), .in1(or_20_out), .out(multiplexer_12_out[4]), .sel(or_19_out));
  or or_20 (or_20_out, and_33_out, and_35_out, and_36_out, and_34_out, and_34_out, and_39_out);
  or or_21 (or_21_out, and_28_out, and_31_out, and_32_out);
  Multiplexer multiplexer_9 (.in0(or_21_out), .in1(or_22_out), .out(multiplexer_12_out[3]), .sel(or_21_out));
  or or_22 (or_22_out, and_33_out, and_35_out, and_36_out, and_34_out, and_39_out);
  Multiplexer multiplexer_10 (.in0(or_23_out), .in1(or_24_out), .out(multiplexer_12_out[2]), .sel(or_23_out));
  or or_23 (or_23_out, and_27_out, and_29_out, and_30_out, and_31_out);
  or or_24 (or_24_out, and_33_out, and_35_out, and_36_out, and_37_out, and_34_out, and_39_out);
  Multiplexer multiplexer_11 (.in0(or_25_out), .in1(or_26_out), .out(multiplexer_12_out[1]), .sel(or_25_out));
  or or_25 (or_25_out, and_28_out, and_32_out);
  or or_26 (or_26_out, and_35_out, and_36_out, and_34_out, and_39_out);
  or or_27 (or_27_out, and_28_out, and_30_out, and_32_out);
  Multiplexer multiplexer_12 (.in0(or_27_out), .in1(or_28_out), .out(multiplexer_12_out[0]), .sel(or_27_out));
  or or_28 (or_28_out, and_35_out, and_37_out, and_34_out, and_39_out);
  Clock clock_1 (.out(clock_1_out));
  Counter #(.max('h1ff), .width(9)) counter_1 (
    .load(1'b1), .clk(clock_1_out), .D(multiplexer_12_out), .Q(counter_1_q));  // open: clr, up, count, carry
  and and_33 (and_33_out, not_15_out, not_16_out, not_17_out, not_18_out, not_19_out, not_20_out, not_21_out, not_22_out, not_23_out);
  and and_34 (and_34_out, counter_1_q[8], not_24_out, counter_1_q[6], counter_1_q[5], counter_1_q[4], not_25_out, counter_1_q[2], not_26_out, not_27_out);
  and and_35 (and_35_out, not_28_out, not_29_out, counter_1_q[6], counter_1_q[5], counter_1_q[4], counter_1_q[3], counter_1_q[2], not_30_out, not_31_out);
  and and_36 (and_36_out, not_32_out, not_33_out, counter_1_q[6], not_34_out, counter_1_q[4], counter_1_q[3], counter_1_q[2], counter_1_q[1], counter_1_q[0]);
  and and_37 (and_37_out, not_35_out, not_36_out, counter_1_q[6], counter_1_q[5], counter_1_q[4], counter_1_q[3], counter_1_q[2], counter_1_q[1], not_37_out);
  and and_38 (and_34_out, not_38_out, not_39_out, not_40_out, not_41_out, not_42_out, not_43_out, counter_1_q[2], not_44_out, counter_1_q[0]);
  and and_39 (and_39_out, counter_1_q[8], counter_1_q[7], counter_1_q[6], not_45_out, counter_1_q[4], counter_1_q[3], not_46_out, counter_1_q[1], counter_1_q[0]);
  and and_40 (and_40_out, not_47_out, not_48_out, not_49_out, not_50_out, counter_1_q[4], counter_1_q[3], counter_1_q[2], counter_1_q[1], counter_1_q[0]);
  not not_15 (not_15_out, counter_1_q[8]);
  not not_16 (not_16_out, counter_1_q[7]);
  not not_17 (not_17_out, counter_1_q[6]);
  not not_18 (not_18_out, counter_1_q[5]);
  not not_19 (not_19_out, counter_1_q[4]);
  not not_20 (not_20_out, counter_1_q[3]);
  not not_21 (not_21_out, counter_1_q[2]);
  not not_22 (not_22_out, counter_1_q[1]);
  not not_23 (not_23_out, counter_1_q[0]);
  not not_24 (not_24_out, counter_1_q[7]);
  not not_25 (not_25_out, counter_1_q[3]);
  not not_26 (not_26_out, counter_1_q[1]);
  not not_27 (not_27_out, counter_1_q[0]);
  not not_28 (not_28_out, counter_1_q[8]);
  not not_29 (not_29_out, counter_1_q[7]);
  not not_30 (not_30_out, counter_1_q[1]);
  not not_31 (not_31_out, counter_1_q[0]);
  not not_32 (not_32_out, counter_1_q[8]);
  not not_33 (not_33_out, counter_1_q[7]);
  not not_34 (not_34_out, counter_1_q[5]);
  not not_35 (not_35_out, counter_1_q[8]);
  not not_36 (not_36_out, counter_1_q[7]);
  not not_37 (not_37_out, counter_1_q[0]);
  not not_38 (not_38_out, counter_1_q[8]);
  not not_39 (not_39_out, counter_1_q[7]);
  not not_40 (not_40_out, counter_1_q[6]);
  not not_41 (not_41_out, counter_1_q[5]);
  not not_42 (not_42_out, counter_1_q[4]);
  not not_43 (not_43_out, counter_1_q[3]);
  not not_44 (not_44_out, counter_1_q[1]);
  not not_45 (not_45_out, counter_1_q[5]);
  not not_46 (not_46_out, counter_1_q[2]);
  not not_47 (not_47_out, counter_1_q[8]);
  not not_48 (not_48_out, counter_1_q[7]);
  not not_49 (not_49_out, counter_1_q[6]);
  not not_50 (not_50_out, counter_1_q[5]);
  // BCD_to_7_Segment_decoder bcd_to_7_segment_decoder_1: pin names not known; wires that end beside it: bcd_to_7_segment_decoder_1_p1, bcd_to_7_segment_decoder_1_p2, bcd_to_7_segment_decoder_1_p3, bcd_to_7_segment_decoder_1_p4, bcd_to_7_segment_decoder_1_p5, bcd_to_7_segment_decoder_1_p6, bcd_to_7_segment_decoder_1_p7, bcd_to_7_segment_decoder_1_p8
  _7_Segment_Display u_7_segment_display_1 (
    .g(bcd_to_7_segment_decoder_1_p1), .f(bcd_to_7_segment_decoder_1_p3), .a(bcd_to_7_segment_decoder_1_p6),
    .b(bcd_to_7_segment_decoder_1_p8), .e(bcd_to_7_segment_decoder_1_p2), .d(bcd_to_7_segment_decoder_1_p4),
    .c(bcd_to_7_segment_decoder_1_p7));  // open: dp
  // BCD_to_7_Segment_decoder bcd_to_7_segment_decoder_2: pin names not known; wires that end beside it: bcd_to_7_segment_decoder_2_p1, bcd_to_7_segment_decoder_2_p2, bcd_to_7_segment_decoder_2_p3, bcd_to_7_segment_decoder_2_p4, bcd_to_7_segment_decoder_2_p5, bcd_to_7_segment_decoder_2_p6, bcd_to_7_segment_decoder_2_p7, bcd_to_7_segment_decoder_2_p8
  // Binary_to_BCD_converter binary_to_bcd_converter_1: pin names not known; wires that end beside it: counter_1_q, in_6, bcd_to_7_segment_decoder_1_p5, bcd_to_7_segment_decoder_2_p5, binary_to_bcd_converter_1_p5
  _7_Segment_Display u_7_segment_display_2 (
    .g(bcd_to_7_segment_decoder_2_p1), .f(bcd_to_7_segment_decoder_2_p3), .a(bcd_to_7_segment_decoder_2_p6),
    .b(bcd_to_7_segment_decoder_2_p8), .e(bcd_to_7_segment_decoder_2_p2), .d(bcd_to_7_segment_decoder_2_p4),
    .c(bcd_to_7_segment_decoder_2_p7));  // open: dp
  // BCD_to_7_Segment_decoder bcd_to_7_segment_decoder_3: pin names not known; wires that end beside it: bcd_to_7_segment_decoder_3_p1, bcd_to_7_segment_decoder_3_p2, bcd_to_7_segment_decoder_3_p3, bcd_to_7_segment_decoder_3_p4, binary_to_bcd_converter_1_p5, bcd_to_7_segment_decoder_3_p6, bcd_to_7_segment_decoder_3_p7, bcd_to_7_segment_decoder_3_p8
  _7_Segment_Display u_7_segment_display_3 (
    .g(bcd_to_7_segment_decoder_3_p1), .f(bcd_to_7_segment_decoder_3_p3), .a(bcd_to_7_segment_decoder_3_p6),
    .b(bcd_to_7_segment_decoder_3_p8), .e(bcd_to_7_segment_decoder_3_p2), .d(bcd_to_7_segment_decoder_3_p4),
    .c(bcd_to_7_segment_decoder_3_p7));  // open: dp

  // Notes on the sheet:
  //   B
  //   D
  //   E
  //   B
  //   D
  //   E
  //   A
  //   B
  //   C
  //   D
  //   E
  //   lineas de seleccion A yC
  //   lineas de seleccion A yC
  //   lineas de seleccion A yC
  //   B'D'E'
  //   B'D'E'
  //   BD
  //   B'D'
  //   BE
  //   B'D'E'
  //   B'DE
  //   B'D'
  //   BDE
  //   B'DE'
  //   BD'
  //   D'E'
  //   DE
  //   D'E'
  //   B'E
  //   B'D'
  //   B'D'E' + BD
  //   B'D' + BE
  //   B'D'E
  //   DE
  //   B'D'E' + B'DE
  //   B'D'E' + B'DE
  //   BD' + D'E'
  //   F4
  //   ABC'D'E
  //   A'BC'D
  //   A'BDE'
  //   A'BCD'
  //   ACDE
  //   AB'CE
  //   BDE + BD’E’ 
  //   B'D'E + DE
  //   DE + B'D'E'
  //   F5
  //   F1
  //   F2
  //   F3
  //   f1
  //   f2
  //   f3
  //   f4
  //   f4
  //   f5
  //   124
  //   95
  //   62
  //   5
  //   475
  //   31
  //   0
  //   372
endmodule
